// Logisim project Ashesi_Vending_Machine.circ as structural Verilog
module main (
);

  wire clock_1_out, In5_out, In10_out, In25_out, or_1_out, Reset_out, Restock1_out, Restock2_out,
       Restock3_out, Vend1_out, Vend2_out, Vend3_out, vending_1_dispense01, vending_1_dispense02,
       vending_1_dispense03, vending_1_empty01, vending_1_empty02, vending_1_empty03;
  wire [3:0] binary_to_bcd_converter_1_p2, binary_to_bcd_converter_1_p4, vending_1_changebcd_2,
       vending_1_depositedbcd_2, vending_1_prod01, vending_1_prod01_2, vending_1_prod02, vending_1_prod02_2,
       vending_1_prod03, vending_1_prod03_2;
  wire [7:0] binary_to_bcd_converter_1_p1, vending_1_changebcd, vending_1_depositedbcd;
  wire [7:4] binary_to_bcd_converter_1_p3;

  Button Vend3 (.out(Vend3_out));
  Hex_Digit_Display Total (.value(binary_to_bcd_converter_1_p3));  // open: dp
  Hex_Digit_Display TotalMoney (.value(binary_to_bcd_converter_1_p2));  // open: dp
  Clock clock_1 (.out(clock_1_out));
  Button Vend2 (.out(Vend2_out));
  Hex_Digit_Display hex_digit_display_1 (.value(binary_to_bcd_converter_1_p4));  // open: dp
  Button In5 (.out(In5_out));
  Button In10 (.out(In10_out));
  Button In25 (.out(In25_out));
  Button Vend1 (.out(Vend1_out));
  Button Restock1 (.out(Restock1_out));
  Button Restock2 (.out(Restock2_out));
  Button Restock3 (.out(Restock3_out));
  Button Reset (.out(Reset_out));
  Hex_Digit_Display hex_digit_display_2 (.value(vending_1_depositedbcd_2));  // open: dp
  Hex_Digit_Display hex_digit_display_3 (.value(vending_1_depositedbcd[7:4]));  // open: dp
  Hex_Digit_Display hex_digit_display_4 (.value(vending_1_depositedbcd[3:0]));  // open: dp
  Hex_Digit_Display hex_digit_display_5 (.value(vending_1_changebcd_2));  // open: dp
  Hex_Digit_Display hex_digit_display_6 (.value(vending_1_changebcd[7:4]));  // open: dp
  Hex_Digit_Display hex_digit_display_7 (.value(vending_1_changebcd[3:0]));  // open: dp
  Vending vending_1 (
    .In5(In5_out), .In10(In10_out), .In25(In25_out), .clk(clock_1_out), .Vend01(Vend1_out),
    .Vend02(Vend2_out), .Vend03(Vend3_out), .Restock01(Restock1_out), .Restock02(Restock2_out),
    .Restock03(Restock3_out), .Rst(Reset_out),
    .DepositedBCD({vending_1_depositedbcd_2, vending_1_depositedbcd}),
    .ChangeBCD({vending_1_changebcd_2, vending_1_changebcd}),
    .Prod01({vending_1_prod01_2, vending_1_prod01}), .Prod02({vending_1_prod02_2, vending_1_prod02}),
    .Prod03({vending_1_prod03_2, vending_1_prod03}), .Empty01(vending_1_empty01),
    .Empty02(vending_1_empty02), .Empty03(vending_1_empty03), .Dispense01(vending_1_dispense01),
    .Dispense02(vending_1_dispense02), .Dispense03(vending_1_dispense03));
  LED SoldOut3 (.in(vending_1_empty03));
  Hex_Digit_Display hex_digit_display_8 (.value(vending_1_prod01_2));  // open: dp
  LED SoldOut1 (.in(vending_1_empty01));
  LED SoldOut2 (.in(vending_1_empty02));
  LED Dispense2 (.in(vending_1_dispense02));
  LED Dispense3 (.in(vending_1_dispense03));
  Hex_Digit_Display hex_digit_display_9 (.value(vending_1_prod01));  // open: dp
  Hex_Digit_Display hex_digit_display_10 (.value(vending_1_prod02_2));  // open: dp
  LED Dispense1 (.in(vending_1_dispense01));
  Hex_Digit_Display hex_digit_display_11 (.value(vending_1_prod02));  // open: dp
  Hex_Digit_Display hex_digit_display_12 (.value(vending_1_prod03_2));  // open: dp
  or or_1 (or_1_out, vending_1_dispense01, vending_1_dispense02, vending_1_dispense03);
  Hex_Digit_Display hex_digit_display_13 (.value(vending_1_prod03));  // open: dp
  // Binary_to_BCD_converter #(.binvalue(8)) binary_to_bcd_converter_1: pin names not known; wires that end beside it: binary_to_bcd_converter_1_p1, binary_to_bcd_converter_1_p2, binary_to_bcd_converter_1_p3, binary_to_bcd_converter_1_p4
  totalCalc totalcalc_1 (.ifVend(or_1_out), .clk(clock_1_out), .binaryTotal(binary_to_bcd_converter_1_p1));

  // Notes on the sheet:
  //   Total
  //   Deposited
  //   Change
  //   Prod01
  //   Prod02
  //   Prod03
endmodule

module Activator (
  input  [7:0] InCash,
  input  [7:0] in_2,
  input  clk,
  input  rst,
  output [11:0] DepositedBCD,
  output Activate,
  output [11:0] ChangeBCD,
  output Ena
);

  wire binary_to_bcd_converter_1_p1, comparator_1_eq, comparator_1_gt, comparator_2_eq, not_1_out;
  wire [3:0] binary_to_bcd_converter_2_p2, binary_to_bcd_converter_2_p3, binary_to_bcd_converter_2_p4;
  wire [7:0] multiplexer_1_out, subtractor_1_out;

  // Binary_to_BCD_converter #(.binvalue(8)) binary_to_bcd_converter_1: pin names not known; wires that end beside it: binary_to_bcd_converter_1_p1, binary_to_bcd_converter_1_p1, InCash, DepositedBCD[11:8], DepositedBCD[7:4], DepositedBCD[3:0]
  Comparator comparator_1 (.a(InCash), .b(8'h4b), .gt(comparator_1_gt), .eq(comparator_1_eq), .lt(Ena));
  Multiplexer #(.width(8)) multiplexer_1 (.in0(8'h4b), .in1(InCash), .out(multiplexer_1_out), .sel(comparator_1_gt));
  Subtractor subtractor_1 (.a(multiplexer_1_out), .b(8'h4b), .out(subtractor_1_out));  // open: bin, bout
  or or_1 (Activate, comparator_1_gt, comparator_1_eq);
  // Binary_to_BCD_converter #(.binvalue(8)) binary_to_bcd_converter_2: pin names not known; wires that end beside it: subtractor_1_out, binary_to_bcd_converter_2_p2, binary_to_bcd_converter_2_p3, binary_to_bcd_converter_2_p4
  Comparator #(.mode("unsigned")) comparator_2 (.a(InCash), .b(in_2), .eq(comparator_2_eq));  // open: gt, lt
  not not_1 (not_1_out, comparator_2_eq);
  Register #(.width(12)) register_1 (
    .D({binary_to_bcd_converter_2_p2, binary_to_bcd_converter_2_p3, binary_to_bcd_converter_2_p4}),
    .en(not_1_out), .clk(clk), .Q(ChangeBCD), .clr(rst));

  // Notes on the sheet:
  //   Activator
endmodule

module Bank (
  input  In5,
  input  In10,
  input  In25,
  input  Ena,
  input  Rst,
  output [7:0] OutAcc
);

  wire or_1_out;
  wire [1:0] priority_encoder_1_out;
  wire [7:0] adder_1_out, multiplexer_1_out;

  or or_1 (or_1_out, In5, In10, In25);
  Multiplexer #(.select(2), .width(8)) multiplexer_1 (
    .in0({8{1'b0}}), .in1(8'h5), .in2(8'ha), .in3(8'h19), .out(multiplexer_1_out),
    .sel(priority_encoder_1_out));
  Priority_Encoder #(.select(2)) priority_encoder_1 (
    .in0(1'b1), .in1(In5), .in2(In10), .in3(In25), .out(priority_encoder_1_out), .en_in(Ena));  // open: gs, en_out
  Register #(.trigger("falling")) register_1 (.D(adder_1_out), .en(Ena), .clk(or_1_out), .Q(OutAcc), .clr(Rst));
  Adder adder_1 (.a(OutAcc), .b(multiplexer_1_out), .out(adder_1_out));  // open: cin, cout

  // Notes on the sheet:
  //   Bank
endmodule

module Dispenser (
  input  Activate,
  input  Vend01,
  input  Vend02,
  input  Vend03,
  input  Restock01,
  input  Restock02,
  input  Restock03,
  output [7:0] Avail01,
  output [7:0] Avail02,
  output [7:0] Avail03,
  output Empty01,
  output Empty02,
  output Empty03,
  output Disp01,
  output Disp02,
  output Disp03
);

  wire demultiplexer_1_out1, demultiplexer_1_out2, demultiplexer_1_out3;
  wire [1:0] priority_encoder_1_out;

  Demultiplexer #(.select(2)) demultiplexer_1 (
    .out1(demultiplexer_1_out1), .out2(demultiplexer_1_out2), .out3(demultiplexer_1_out3), .in(Activate),
    .sel(priority_encoder_1_out));  // open: out0
  Priority_Encoder #(.select(2)) priority_encoder_1 (
    .in0(1'b1), .in1(Vend01), .in2(Vend02), .in3(Vend03), .out(priority_encoder_1_out), .en_in(1'b1));  // open: gs, en_out
  Product product_1 (
    .Restock(Restock01), .Vend(demultiplexer_1_out1), .Avail_BCD(Avail01), .Empty(Empty01), .Dispensed(Disp01));
  Product product_2 (
    .Restock(Restock02), .Vend(demultiplexer_1_out2), .Avail_BCD(Avail02), .Empty(Empty02), .Dispensed(Disp02));
  Product product_3 (
    .Restock(Restock03), .Vend(demultiplexer_1_out3), .Avail_BCD(Avail03), .Empty(Empty03), .Dispensed(Disp03));

  // Notes on the sheet:
  //   Dispenser
endmodule

module Product (
  input  Restock,
  input  Vend,
  output [7:0] Avail_BCD,
  output Empty,
  output Dispensed
);

  wire not_1_out, or_1_out;
  wire [3:0] counter_1_q;

  Counter #(.max('hf), .ongoal("stay"), .width(4)) counter_1 (
    .load(Restock), .up(1'b0), .count(not_1_out), .clk(or_1_out), .D(4'b1111), .carry(Empty), .Q(counter_1_q));  // open: clr
  not not_1 (not_1_out, Empty);
  or or_1 (or_1_out, Restock, Vend);
  and and_1 (Dispensed, ~Empty, Vend);  // AND_Gate
  // Binary_to_BCD_converter #(.binvalue(4)) binary_to_bcd_converter_1: pin names not known; wires that end beside it: counter_1_q, Avail_BCD[7:4], Avail_BCD[3:0]

  // Notes on the sheet:
  //   Product
endmodule

module Vending (
  input  In5,
  input  In10,
  input  In25,
  input  clk,
  input  Vend01,
  input  Vend02,
  input  Vend03,
  input  Restock01,
  input  Restock02,
  input  Restock03,
  input  Rst,
  output [11:0] DepositedBCD,
  output [11:0] ChangeBCD,
  output [7:0] Prod01,
  output [7:0] Prod02,
  output [7:0] Prod03,
  output Empty01,
  output Empty02,
  output Empty03,
  output Dispense01,
  output Dispense02,
  output Dispense03
);

  wire activator_1_activate, activator_1_ena, or_1_out, or_2_out;
  wire [7:0] bank_1_outacc;

  or or_1 (or_1_out, Rst, or_2_out);
  Bank bank_1 (.In5(In5), .In10(In10), .In25(In25), .Ena(activator_1_ena), .Rst(or_1_out), .OutAcc(bank_1_outacc));
  Activator activator_1 (
    .InCash(bank_1_outacc), .clk(clk), .rst(Rst), .DepositedBCD(DepositedBCD),
    .Activate(activator_1_activate), .ChangeBCD(ChangeBCD), .Ena(activator_1_ena));  // open: in_2
  Dispenser dispenser_1 (
    .Activate(activator_1_activate), .Vend01(Vend01), .Vend02(Vend02), .Vend03(Vend03),
    .Restock01(Restock01), .Restock02(Restock02), .Restock03(Restock03), .Avail01(Prod01), .Avail02(Prod02),
    .Avail03(Prod03), .Empty01(Empty01), .Empty02(Empty02), .Empty03(Empty03), .Disp01(Dispense01),
    .Disp02(Dispense02), .Disp03(Dispense03));
  // OR_Gate or_2 has open pins: out=or_2_out

  // Notes on the sheet:
  //   Vending
endmodule

module totalCalc (
  input  ifVend,
  input  clk,
  output [7:0] binaryTotal
);

  wire [7:0] adder_1_out;

  Adder adder_1 (.a(binaryTotal), .b(8'h4b), .out(adder_1_out));  // open: cin, cout
  Register register_1 (.D(adder_1_out), .en(ifVend), .clk(clk), .Q(binaryTotal));  // open: clr
endmodule
